// Logisim project ALu decoder.circ as structural Verilog: 1 circuit, main circuit main
module main (
  input  A,
  input  B,
  input  C,
  input  D,
  output out_5,
  output out_6,
  output out_7,
  output nXOR_EN,
  output nOR_EN,
  output _AND_EN,
  output out_11
);

  wire and_1_out, not_1_out, not_2_out, not_3_out, or_2_out, or_3_out, or_4_out, or_5_out, or_7_out;

  not not_1 (not_1_out, A);
  not not_2 (not_2_out, C);
  not not_3 (not_3_out, D);
  and and_1 (and_1_out, A, B);
  not not_4 (out_6, and_1_out);
  or or_1 (out_7, and_1_out, C);
  or or_2 (or_2_out, not_2_out, not_3_out);
  or or_3 (or_3_out, not_2_out, D);
  or or_4 (or_4_out, C, not_3_out);
  or or_5 (or_5_out, C, D);
  or or_6 (out_5, not_2_out, and_1_out);
  or or_7 (or_7_out, not_1_out, B);
  or or_8 (nXOR_EN, or_7_out, or_2_out);
  or or_9 (nOR_EN, or_7_out, or_3_out);
  or or_10 (_AND_EN, or_7_out, or_4_out);
  or or_11 (out_11, or_7_out, or_5_out);

  // Notes on the sheet:
  //   !A
  //   !C
  //   !D
  //   ~Right EN
  //   ~ADDER_EN
  //   ~LEFT_EN
  //   ~NAND EN
endmodule
